# Fritzing sketch TeleInfo_Node_PCB (saved by Fritzing 0.8.7b)
circuit board: 4.74103cm x 1.89812cm

parts:
  C1 = Capacitor [package=cap-pth-small2]
  C2 = Capacitor [package=cap-pth-small2]
  XTAL = Crystal [frequency="8 MHz" package=THT]
  OPTO = TLP621 [package=THT]
  R2 = Resistor [tolerance=±5% resistance=220 package=THT]
  ATtiny85 = attiny85 [package=dip]
  LED1 = LED - 5mm [color="Red (633nm)" package="5 mm [THT]"]
  R3 = Resistor [tolerance=±5% resistance=220 package=THT]
  TX = RF-LINK_TX [package=rf-link_tx]
  R1 = Resistor [tolerance=±5% resistance=220 package=THT]

nets:
  N1: C1.1, XTAL.pin_1, ATtiny85.Pin_2
  GND: C1.2, C2.2, OPTO.Pin_3, ATtiny85.Pin_4, LED1.cathode, TX.GND
  N2: C2.1, XTAL.pin_0, ATtiny85.Pin_3
  EDF -: OPTO.Pin_1
  N3: OPTO.Pin_2, R1.Pin_0
  N4: OPTO.Pin_4, ATtiny85.Pin_5
  N5: R2.Pin_0, R1.Pin_1
  EDF +: R2.Pin_1
  N6: ATtiny85.Pin_7, R3.Pin_1, TX.DATA
  5V: ATtiny85.Pin_8, TX.+5V
  N7: LED1.anode, R3.Pin_0
  ANT: TX.ANT

notes:
  TeleInfo by TTK
  5V
  GND
  RST
  ANT
